# Fritzing sketch fritzing (saved by Fritzing 0.9.3b)
circuit board: 5.8cm x 2.7cm
breadboards: 1

parts:
  ESP-01 = ESP8266 WiFi Module [part_number=ESP8266]
  HX-711 = HX711 Weighing Sensor Module
  1700 = Voltage Regulator [package=to-92]
  U3 = attiny85 [package=dip]
  R050 = Resettable Fuse PTC [package=ptc]
  R1 = Resistor [tolerance=±5% resistance=10k package=THT]
  R2 = Resistor [tolerance=±5% resistance=10k package=THT]
  J1 = female pin header, 6 pins [form="♀ (female)"]
  J2 = female pin header, 2 pins [form="♀ (female)"]
  R4 = Resistor [tolerance=±5% resistance=10k package=THT]
  R53 = Resistor [tolerance=±5% resistance=10k package=THT]
  R54 = Resistor [tolerance=±5% resistance=100k package=THT]
  R55 = Resistor [tolerance=±5% resistance=470k package=THT]
  U4 = Molex Picoblade Series Header [part_number=0532610219 package=Picoblade-53261-0219]
  Pad1 = Pad [width=2.070731054602498 height=0.82396141526075872 connect=center]
  Pad2 = Pad [width=2.070731054602498 height=0.82396141526075872 connect=center]

nets:
  3.3V: ESP-01.VCC, ESP-01.CH_PD, HX-711.VCC, U3.Pin_8, R050.1, R1.Pin_1, R2.Pin_1, R4.Pin_0, R53.Pin_1
  N1: ESP-01.GPIO_0, U3.Pin_5, R1.Pin_0, J2.pin2
  N2: ESP-01.RST, U3.Pin_6, R53.Pin_0
  N3: ESP-01.GPIO_2, U3.Pin_7, R2.Pin_0, J2.pin1
  GND: ESP-01.GND, HX-711.GND, 1700.GND, U3.Pin_4, R54.Pin_0, U4.2, Pad2.pad
  RXD: ESP-01.TXD, R54.Pin_1, R55.Pin_0
  N4: HX-711.DO/RX, U3.Pin_2
  N5: HX-711.CK/TX, U3.Pin_3
  N6: HX-711.E+, J1.pin1
  N7: HX-711.E-, J1.pin2
  N8: HX-711.A+, J1.pin3
  N9: HX-711.A-, J1.pin4
  N10: HX-711.B+, J1.pin5
  N11: HX-711.B-, J1.pin6
  N12: 1700.IN, R55.Pin_1, U4.1, Pad1.pad
  N13: 1700.OUT, R050.2
  N14: U3.Pin_1, R4.Pin_1

notes:
  SDA
  SCL

custom parts:
  ESP8266 WiFi Module: Generic WiFi Module based on the ESP8266 with onboard PCB antenna and UART communications
